// Digital circuit cpu.dig as structural Verilog
module cpu (
  input  [7:0] M,
  input  [7:0] N,
  input  clk,
  input  [13:0] progIn,
  input  progLoad,
  input  result,
  input  reset,
  input  start,
  output [7:0] \output ,
  output valid,
  output done
);

  wire and_2_out, and_3_out, and_5_out, and_6_out, and_9_out, and_11_out, and_12_out, and_13_out, and_14_out,
       and_15_out, and_16_out, and_17_out, and_18_out, and_19_out, as, bs, comparator_3_eq, comparator_6_eq,
       comparator_7_eq, comparator_8_eq, comparator_8_gt, comparator_8_lt, comparator_9_eq, cs, delay_3_out,
       ds, eFlag, gFlag, jump, lcm, lFlag, multiplexer_22_out, or_1_out, or_2_out, or_3_out, or_4_out,
       or_5_out, or_6_out, or_8_out, or_9_out, or_10_out, or_13_out, or_14_out, or_15_out, or_17_out,
       or_18_out, or_19_out, prime_d, re, readRam, rehold, resetstop, restop, resulthold, sigComp, sigDiv,
       sigJump, sigJump_eq, sigJump_eq__gt, sigJump_eq__lt, sigJump_gt, sigJump_lt, sigPrime, sigRam, st,
       starthold;
  wire [0:0] or_16_out;
  wire [1:0] b_store_d, c_store_d, d_ff_10_q, d_ff_11_q, d_ff_12_q, d_store_d;
  wire [3:0] abcd_store_d;
  wire [4:0] a_store_d, d_ff_9_q;
  wire [5:0] d_ff_3_q, d_ff_5_q, delay_2_out, delay_4_out, multiplexer_14_out_2, multiplexer_15_out, opcode;
  wire [7:0] A, add_1_s, add_2_s, ads, and_10_out, B, barrelshifter_1_out, barrelshifter_2_out,
       barrelshifter_3_out, barrelshifter_4_out, C, counter_1_out, counter_2_out, counter_3_out,
       counter_4_out, D, d_ff_2_q, d_ff_7_q, delay_1_out, div_1_q, div_1_r, div_2_r, LCM_m_n___0_7,
       LCM_m_n___8_15, mul_1_mul, multiplexer_1_out, multiplexer_2_out, multiplexer_3_out, multiplexer_4_out,
       multiplexer_5_out, multiplexer_6_out, multiplexer_7_out, multiplexer_8_out, multiplexer_9_out,
       multiplexer_10_out, multiplexer_12_out, multiplexer_13_out, multiplexer_14_out, multiplexer_19_out,
       multiplexer_20_out, multiplexer_23_out, multiplexer_24_out, multiplexer_25_out, multiplexer_26_out,
       multiplexer_27_out, multiplexer_28_out, Noperand, not_1_out, operand, or_11_out, out, output_t, rA,
       ramdualaccess_3_d2, rmini2, rom_1_d, sub_1_s, xor_1_out;
  wire [11:0] rom_2_d;
  wire [13:0] ramdualaccess_3_d1;
  wire [13:8] ramdualaccess_3_d2_2;

  Counter #(.Bits(8)) counter_1 (.en(rehold), .C(clk), .clr(~rehold), .out(counter_1_out));  // open: ovf
  Counter #(.Bits(8)) counter_2 (.en(rehold), .C(clk), .clr(~rehold), .out(counter_2_out));  // open: ovf
  Comparator #(.Bits(8)) comparator_1 (.a(counter_1_out), .b(8'h10), .eq(resetstop));  // open: gt, lt
  Multiplexer #(.Bits(8)) multiplexer_1 (.sel(lcm), .in_0(A), .in_1(LCM_m_n___0_7), .out(multiplexer_1_out));
  Comparator #(.Bits(8)) comparator_2 (.a(counter_2_out), .b(8'h10), .eq(resetstop));  // open: gt, lt
  and and_1 (starthold, ~start, or_1_out);  // And
  or or_1 (or_1_out, start, and_2_out);
  D_FF d_ff_1 (.D(start), .C(clk), .Q(st));  // open: nQ
  Comparator #(.Bits(6)) comparator_3 (.a(opcode), .b({6{1'b1}}), .eq(comparator_3_eq));  // open: gt, lt
  Multiplexer #(.Bits(8)) multiplexer_2 (.sel(or_2_out), .in_0({8{1'b0}}), .in_1(add_1_s), .out(multiplexer_2_out));
  or or_2 (or_2_out, progLoad, starthold);
  Multiplexer #(.Bits(8)) multiplexer_3 (.sel(lcm), .in_0(operand), .in_1(8'hf), .out(multiplexer_3_out));
  Multiplexer #(.Bits(8)) multiplexer_4 (
    .sel(rehold), .in_0(multiplexer_1_out), .in_1({8{1'b0}}), .out(multiplexer_4_out));
  Multiplexer #(.Bits(8)) multiplexer_5 (.sel(lcm), .in_0(A), .in_1(LCM_m_n___8_15), .out(multiplexer_5_out));
  Multiplexer #(.Bits(8)) multiplexer_6 (
    .sel(rehold), .in_0(multiplexer_5_out), .in_1({8{1'b0}}), .out(multiplexer_6_out));
  and and_2 (and_2_out, ~re, ~comparator_3_eq, or_1_out);  // And
  Multiplexer #(.Bits(8)) multiplexer_7 (.sel(jump), .in_0(multiplexer_2_out), .in_1(operand), .out(multiplexer_7_out));
  Multiplexer #(.Bits(8)) multiplexer_8 (.sel(lcm), .in_0(operand), .in_1(8'he), .out(multiplexer_8_out));
  Add #(.Bits(8)) add_1 (.a(d_ff_2_q), .b(8'h1), .c_i(1'b0), .s(add_1_s));  // open: c_o
  Multiplexer #(.Bits(8)) multiplexer_9 (
    .sel(rehold), .in_0(multiplexer_3_out), .in_1(counter_1_out), .out(multiplexer_9_out));
  Multiplexer #(.Bits(8)) multiplexer_10 (
    .sel(rehold), .in_0(multiplexer_8_out), .in_1(counter_2_out), .out(multiplexer_10_out));
  D_FF #(.Bits(8)) d_ff_2 (.D(multiplexer_7_out), .C(clk), .Q(d_ff_2_q));  // open: nQ
  or or_3 (or_3_out, rehold, lcm, sigRam);
  or or_4 (or_4_out, rehold, lcm, sigRam);
  Multiplexer #(.Bits(8)) multiplexer_11 (.sel(lcm), .in_0(counter_3_out), .in_1({4'b0000, operand[3:0]}), .out(ads));
  Counter #(.Bits(8)) counter_3 (.en(resulthold), .C(clk), .clr(~resulthold), .out(counter_3_out));  // open: ovf
  Multiplexer #(.Bits(8)) multiplexer_12 (
    .sel(lcm), .in_0(counter_4_out), .in_1({4'b0000, operand[7:4]}), .out(multiplexer_12_out));
  Counter #(.Bits(8)) counter_4 (.en(resulthold), .C(clk), .clr(~resulthold), .out(counter_4_out));  // open: ovf
  or or_5 (or_5_out, resulthold, readRam);
  or or_6 (or_6_out, resulthold, readRam);
  and and_3 (and_3_out, or_8_out, ~re);  // And
  or or_7 (resulthold, result, and_5_out);
  RAMDualAccess #(.AddrBits(8), .Bits(8)) ramdualaccess_1 (
    .str(or_3_out), .C(clk), .ld(or_5_out), .A1(multiplexer_9_out), .Din1(multiplexer_4_out), .A2(ads),
    .D1(rA), .D2(output_t));
  Comparator #(.Bits(8)) comparator_4 (.a(counter_3_out), .b(8'h11), .eq(restop));  // open: gt, lt
  RAMDualAccess #(.AddrBits(8), .Bits(8)) ramdualaccess_2 (
    .str(or_4_out), .C(clk), .ld(or_6_out), .A1(multiplexer_10_out), .Din1(multiplexer_6_out),
    .A2(multiplexer_12_out), .D2(rmini2));  // open: D1
  and and_4 (valid, or_8_out, ~st);  // And
  or or_8 (or_8_out, and_3_out, st);
  and and_5 (and_5_out, ~restop, resulthold);  // And
  Comparator #(.Bits(8)) comparator_5 (.a(counter_4_out), .b(8'h11), .eq(restop));  // open: gt, lt
  RAMDualAccess #(.AddrBits(8), .Bits(14)) ramdualaccess_3 (
    .str(progLoad), .C(clk), .ld(starthold), .A1(d_ff_2_q), .Din1(progIn), .A2(operand),
    .D1(ramdualaccess_3_d1), .D2({ramdualaccess_3_d2_2, ramdualaccess_3_d2}));
  D_FF #(.Bits(6)) d_ff_3 (.D(opcode), .C(clk), .Q(d_ff_3_q));  // open: nQ
  Multiplexer #(.Bits(8)) multiplexer_13 (.sel(resulthold), .in_0({8{1'b0}}), .in_1(out), .out(multiplexer_13_out));
  Delay #(.Bits(8)) delay_1 (.in(multiplexer_13_out), .out(delay_1_out));
  Multiplexer #(.Bits(14)) multiplexer_14 (
    .sel(starthold), .in_0({14{1'b0}}), .in_1(ramdualaccess_3_d1),
    .out({multiplexer_14_out_2, multiplexer_14_out}));
  and and_6 (and_6_out, clk, resulthold);
  Delay #(.Bits(6)) delay_2 (.in(multiplexer_14_out_2), .out(delay_2_out));
  Comparator #(.Bits(6)) comparator_6 (.a(d_ff_3_q), .b(6'b001111), .eq(comparator_6_eq));  // open: gt, lt
  D_FF #(.Bits(8)) d_ff_4 (.D(delay_1_out), .C(and_6_out), .Q(\output ));  // open: nQ
  and and_7 (done, ~re, ~result, ~st, or_9_out, ~progLoad);  // And
  or or_9 (or_9_out, restop, done);
  Multiplexer #(.Bits(6)) multiplexer_15 (.sel(jump), .in_0(delay_2_out), .in_1({6{1'b0}}), .out(multiplexer_15_out));
  D_FF #(.Bits(6)) d_ff_5 (.D(multiplexer_15_out), .C(clk), .Q(d_ff_5_q));  // open: nQ
  Multiplexer #(.Bits(8)) multiplexer_16 (
    .sel(comparator_6_eq), .in_0({8{1'b0}}), .in_1(ramdualaccess_3_d2), .out(Noperand));
  Comparator #(.Bits(8)) comparator_7 (.a(ads), .b(8'he), .eq(comparator_7_eq));  // open: gt, lt
  D_FF d_ff_6 (.D(delay_3_out), .C(clk), .Q(re));  // open: nQ
  Delay delay_3 (.in(reset), .out(delay_3_out));
  D_FF #(.Bits(8)) d_ff_7 (.D(multiplexer_14_out), .C(clk), .Q(d_ff_7_q));  // open: nQ
  Delay #(.Bits(6)) delay_4 (.in(d_ff_5_q), .out(delay_4_out));
  Multiplexer #(.Bits(8)) multiplexer_17 (.sel(comparator_7_eq), .in_0(output_t), .in_1(rmini2), .out(out));
  and and_8 (rehold, ~resetstop, or_10_out);  // And
  or or_10 (or_10_out, re, and_9_out);
  D_FF #(.Bits(8)) d_ff_8 (.D(d_ff_7_q), .C(clk), .Q(operand));  // open: nQ
  Multiplexer #(.Bits(6)) multiplexer_18 (.sel(jump), .in_0(delay_4_out), .in_1({6{1'b0}}), .out(opcode));
  and and_9 (and_9_out, ~resetstop, rehold);  // And
  Seven_Seg_Hex seven_seg_hex_1 (.d(\output [7:4]), .dp(1'b0));
  Seven_Seg_Hex seven_seg_hex_2 (.d(\output [3:0]), .dp(1'b0));
  Add #(.Bits(8)) add_2 (.a(A), .b(B), .c_i(1'b0), .s(add_2_s));  // open: c_o
  Sub #(.Bits(8)) sub_1 (.a(A), .b(B), .c_i(1'b0), .s(sub_1_s));  // open: c_o
  Mul #(.Bits(4)) mul_1 (.a(A[3:0]), .b(B[3:0]), .mul(mul_1_mul));
  Div #(.Bits(8)) div_1 (.a(A), .b(B), .q(div_1_q), .r(div_1_r));
  ROM #(.AddrBits(6), .Bits(8)) rom_1 (.A({A[2:0], B[2:0]}), .sel(as), .D(rom_1_d));
  assign and_10_out = A & B;  // And and_10, 8 bits wide
  assign or_11_out = A | B;  // Or or_11, 8 bits wide
  assign xor_1_out = A ^ B;  // XOr xor_1, 8 bits wide
  BarrelShifter #(.Bits(8)) barrelshifter_1 (.in(A), .shift(B[3:0]), .out(barrelshifter_1_out));
  BarrelShifter #(.Bits(8), .barrelShifterMode("rotate")) barrelshifter_2 (
    .in(A), .shift(B[3:0]), .out(barrelshifter_2_out));
  BarrelShifter #(.Bits(8), .direction("right")) barrelshifter_3 (.in(A), .shift(B[3:0]), .out(barrelshifter_3_out));
  BarrelShifter #(.Bits(8), .barrelShifterMode("rotate"), .direction("right")) barrelshifter_4 (
    .in(A), .shift(B[3:0]), .out(barrelshifter_4_out));
  and and_11 (and_11_out, sigJump_eq, eFlag);
  assign not_1_out = ~A;  // Not not_1, 8 bits wide
  and and_12 (and_12_out, sigJump_gt, gFlag);
  Multiplexer #(.Selector_Bits(5), .Bits(8)) multiplexer_19 (
    .sel(d_ff_9_q), .in_0(operand), .in_1(B), .in_2(C), .in_3(D), .in_4(C), .in_5(Noperand), .in_6(rA),
    .in_7(add_2_s), .in_8(sub_1_s), .in_9(mul_1_mul), .in_10(div_1_q), .in_11(div_1_r), .in_12(rom_1_d),
    .in_13(not_1_out), .in_14(and_10_out), .in_15(or_11_out), .in_16(xor_1_out), .in_17(barrelshifter_1_out),
    .in_18(barrelshifter_2_out), .in_19(barrelshifter_3_out), .in_20(barrelshifter_4_out), .in_21({8{1'b0}}),
    .in_22({8{1'b0}}), .in_23({8{1'b0}}), .in_24({8{1'b0}}), .in_25({8{1'b0}}), .in_26({8{1'b0}}),
    .in_27({8{1'b0}}), .in_28({8{1'b0}}), .in_29({8{1'b0}}), .in_30({8{1'b0}}), .in_31({8{1'b0}}),
    .out(multiplexer_19_out));
  D_FF #(.Bits(5)) d_ff_9 (.D(a_store_d), .C(clk), .Q(d_ff_9_q));  // open: nQ
  or or_12 (jump, and_11_out, and_12_out, and_13_out, and_14_out, and_15_out, and_17_out);
  and and_13 (and_13_out, sigJump, sigJump);
  Multiplexer #(.Bits(8)) multiplexer_20 (
    .sel(re), .in_0(multiplexer_19_out), .in_1({8{1'b0}}), .out(multiplexer_20_out));
  ROM #(.AddrBits(6), .Bits(5)) a_store (.A(opcode), .sel(1'b1), .D(a_store_d));
  and and_14 (and_14_out, sigJump_lt, lFlag);
  or or_13 (or_13_out, as, re);
  Comparator #(.Bits(8)) comparator_8 (.a(A), .b(B), .gt(comparator_8_gt), .eq(comparator_8_eq), .lt(comparator_8_lt));
  Div #(.Bits(8)) div_2 (.a(A), .b(B), .r(div_2_r));  // open: q
  Register #(.Bits(8)) accA (.D(multiplexer_20_out), .C(clk), .en(or_13_out), .Q(A));
  and and_15 (and_15_out, sigJump_eq__gt, or_14_out);
  ROM #(.AddrBits(8)) prime (.A(A), .sel(1'b1), .D(prime_d));
  and and_16 (and_16_out, gFlag, ~re);  // And
  Comparator #(.Bits(8)) comparator_9 (.a(div_2_r), .b({8{1'b0}}), .eq(comparator_9_eq));  // open: gt, lt
  ROM #(.AddrBits(6), .Bits(2)) b_store (.A(opcode), .sel(1'b1), .D(b_store_d));
  ROM #(.AddrBits(6), .Bits(2)) c_store (.A(opcode), .sel(1'b1), .D(c_store_d));
  ROM #(.AddrBits(6), .Bits(2)) d_store (.A(opcode), .sel(1'b1), .D(d_store_d));
  or or_14 (or_14_out, eFlag, gFlag);
  Multiplexer multiplexer_21 (.sel(sigComp), .in_0(and_16_out), .in_1(comparator_8_gt), .out(gFlag));
  and and_17 (and_17_out, sigJump_eq__lt, or_15_out);
  D_FF #(.Bits(2)) d_ff_10 (.D(b_store_d), .C(clk), .Q(d_ff_10_q));  // open: nQ
  D_FF #(.Bits(2)) d_ff_11 (.D(c_store_d), .C(clk), .Q(d_ff_11_q));  // open: nQ
  D_FF #(.Bits(2)) d_ff_12 (.D(d_store_d), .C(clk), .Q(d_ff_12_q));  // open: nQ
  or or_15 (or_15_out, eFlag, gFlag);
  Multiplexer multiplexer_22 (.sel(sigPrime), .in_0(comparator_8_eq), .in_1(prime_d), .out(multiplexer_22_out));
  ROM #(.AddrBits(6), .Bits(4)) abcd_store (.A(opcode), .sel(1'b1), .D(abcd_store_d));
  Multiplexer #(.Selector_Bits(2), .Bits(8)) multiplexer_23 (
    .sel(d_ff_10_q), .in_0({8{1'b0}}), .in_1(operand), .in_2(A), .in_3(D), .out(multiplexer_23_out));
  Multiplexer #(.Selector_Bits(2), .Bits(8)) multiplexer_24 (
    .sel(d_ff_11_q), .in_0({8{1'b0}}), .in_1(A), .in_2(M), .in_3(N), .out(multiplexer_24_out));
  Multiplexer #(.Selector_Bits(2), .Bits(8)) multiplexer_25 (
    .sel(d_ff_12_q), .in_0({8{1'b0}}), .in_1(A), .in_2(M), .in_3(N), .out(multiplexer_25_out));
  and and_18 (and_18_out, eFlag, ~re);  // And
  or or_16 (or_16_out[0], sigComp, sigPrime);
  D_FF #(.Bits(4)) d_ff_13 (.D(abcd_store_d), .C(clk), .Q({as, bs, cs, ds}));  // open: nQ
  and and_19 (and_19_out, lFlag, ~re);  // And
  Multiplexer #(.Bits(8)) multiplexer_26 (
    .sel(re), .in_0(multiplexer_23_out), .in_1({8{1'b0}}), .out(multiplexer_26_out));
  Multiplexer #(.Bits(8)) multiplexer_27 (
    .sel(re), .in_0(multiplexer_24_out), .in_1({8{1'b0}}), .out(multiplexer_27_out));
  Multiplexer #(.Bits(8)) multiplexer_28 (
    .sel(re), .in_0(multiplexer_25_out), .in_1({8{1'b0}}), .out(multiplexer_28_out));
  Multiplexer #(.Selector_Bits(2)) multiplexer_29 (
    .sel({sigDiv, or_16_out[0]}), .in_0(and_18_out), .in_1(multiplexer_22_out), .in_2(comparator_9_eq),
    .in_3(1'b0), .out(eFlag));
  Multiplexer multiplexer_30 (.sel(sigComp), .in_0(and_19_out), .in_1(comparator_8_lt), .out(lFlag));
  Register #(.Bits(8)) AccB (.D(multiplexer_26_out), .C(clk), .en(or_17_out), .Q(B));
  or or_17 (or_17_out, bs, re);
  Register #(.Bits(8)) regC (.D(multiplexer_27_out), .C(clk), .en(or_18_out), .Q(C));
  or or_18 (or_18_out, cs, re);
  Register #(.Bits(8)) regD (.D(multiplexer_28_out), .C(clk), .en(or_19_out), .Q(D));
  or or_19 (or_19_out, ds, re);
  ROM #(.AddrBits(6), .Bits(12)) rom_2 (.A(opcode), .sel(1'b1), .D(rom_2_d));
  D_FF #(.Bits(12)) d_ff_14 (
    .D(rom_2_d), .C(clk),
    .Q({lcm, readRam, sigDiv, sigPrime, sigComp, sigJump_eq__lt, sigJump_eq__gt, sigJump_lt, sigJump_gt, sigJump_eq, sigJump, sigRam}));  // open: nQ
  ROM #(.AddrBits(16), .Bits(8)) OPS30_0F (.A({rmini2, output_t}), .sel(1'b1), .D(LCM_m_n___0_7));
  ROM #(.AddrBits(16), .Bits(8)) OPS30_0E (.A({rmini2, output_t}), .sel(1'b1), .D(LCM_m_n___8_15));

  // Other names for the same wires on the sheet: in[13:0] = progIn; load = progLoad;
  //   operand_addr1[3:0] = operand[3:0]; operand_addr1out[3:0] = operand[3:0]; operand_addr0[3:0] = operand[7:4];
  //   operand_addr0out[3:0] = operand[7:4]; retemp = result

  // Notes on the sheet:
  //   rRAM
  //   Start hold
  //   pRAM
  //   Valid
  //   Result hold
  //   Done
  //   Reset hold
  //   opcode[store ABCD]
  //   opcode[jump]
  //   contents of rom_1 (hex, n*v repeats v):
  //   1,7*0,9*1,2,4,8,10,20,40,80,1,3,9,1b,51,f3,d9,8b,1,4,10,40,a00
  //   ,0,0,0,1,5,19,7d,71,35,9,2d,1,6,24,d8,10,60,40,80,1,7,31,57,61
  //   ,a7,91,f7
  //   opcode[prime,comp, | ]
  //   contents of a_store (hex, n*v repeats v):
  //   0,0,0,1,0,0,2,0,3,5*0,4,5,6,15*0,7,8,9,a,b,c,0,0,d,e,f,10,11,12
  //   ,13,14
  //   contents of prime (hex, n*v repeats v):
  //   0,0,1,1,0,1,0,1,0,0,0,1,0,1,0,0,0,1,0,1,0,0,0,1,5*0,1,0,1,5*0
  //   ,1,0,0,0,1,0,1,0,0,0,1,5*0,1,5*0,1,0,1,5*0,1,0,0,0,1,0,1,5*0,1
  //   ,0,0,0,1,5*0,1,7*0,1,0,0,0,1,0,1,0,0,0,1,0,1,0,0,0,1,13*0,1,0,0,0
  //   ,1,5*0,1,0,1,9*0,1,0,1,5*0,1,5*0,1,0,0,0,1,5*0,1,5*0,1,0,1,9*0
  //   ,1,0,1,0,0,0,1,0,1,11*0,1,11*0,1,0,0,0,1,0,1,0,0,0,1,5*0,1,0,1
  //   ,9*0,1
  //   contents of b_store (hex, n*v repeats v):
  //   0,0,1,0,2,8*0,3
  //   contents of c_store (hex, n*v repeats v):
  //   5*0,1,0,0,0,2,3,0,0,2
  //   contents of d_store (hex, n*v repeats v):
  //   7*0,1,0,0,0,2,3,3
  //   contents of abcd_store (hex, n*v repeats v):
  //   0,8,4,8,4,2,8,1,8,2,2,1,1,3,c,8,8,15*0,14*8
  //   opcode[LCM]
  //   contents of rom_2 (hex, n*v repeats v):
  //   16*0,400,1,2,4,8,10,20,40,24*0,80,100,200,800
  //   contents of OPS30_0F (hex, n*v repeats v):
  //   257*0,1,2,3,4,5,6,7,8,9,a,b,c,d,e,f,10,11,12,13,14,15,16,17,18
  //   ,19,1a,1b,1c,1d,1e,1f,20,21,22,23,24,25,26,27,28,29,2a,2b,2c,2d
  //   ,2e,2f,30,31,32,33,34,35,36,37,38,39,3a,3b,3c,3d,3e,3f,40,41,42
  //   ,43,44,45,46,47,48,49,4a,4b,4c,4d,4e,4f,50,51,52,53,54,55,56,57
  //   ,58,59,5a,5b,5c,5d,5e,5f,60,61,62,63,64,65,66,67,68,69,6a,6b,6c
  //   ,6d,6e,6f,70,71,72,73,74,75,76,77,78,79,7a,7b,7c,7d,7e,7f,80,81
  //   ,82,83,84,85,86,87,88,89,8a,8b,8c,8d,8e,8f,90,91,92,93,94,95,96
  //   ,97,98,99,9a,9b,9c,9d,9e,9f,a0,a1,a2,a3,a4,a5,a6,a7,a8,a9,aa,ab
  //   ,ac,ad,ae,af,b0,b1,b2,b3,b4,b5,b6,b7,b8,b9,ba,bb,bc,bd,be,bf,c0
  //   ,c1,c2,c3,c4,c5,c6,c7,c8,c9,ca,cb,cc,cd,ce,cf,d0,d1,d2,d3,d4,d5
  //   ,d6,d7,d8,d9,da,db,dc,dd,de,df,e0,e1,e2,e3,e4,e5,e6,e7,e8,e9,ea
  //   ,eb,ec,ed,ee,ef,f0,f1,f2,f3,f4,f5,f6,f7,f8,f9,fa,fb,fc,fd,fe,ff
  //   ,0,2,2,6,4,a,6,e,8,12,a,16,c,1a,e,1e,10,22,12,26,14,2a,16,2e,18
  //   ,32,1a,36,1c,3a,1e,3e,20,42,22,46,24,4a,26,4e,28,52,2a,56,2c,5a
  //   ,2e,5e,30,62,32,66,34,6a,36,6e,38,72,3a,76,3c,7a,3e,7e,40,82,42
  //   ,86,44,8a,46,8e,48,92,4a,96,4c,9a,4e,9e,50,a2,52,a6,54,aa,56,ae
  //   ,58,b2,5a,b6,5c,ba,5e,be,60,c2,62,c6,64,ca,66,ce,68,d2,6a,d6,6c
  //   ,da,6e,de,70,e2,72,e6,74,ea,76,ee,78,f2,7a,f6,7c,fa,7e,fe,80,2
  //   ,82,6,84,a,86,e,88,12,8a,16,8c,1a,8e,1e,90,22,92,26,94,2a,96,2e
  //   ,98,32,9a,36,9c,3a,9e,3e,a0,42,a2,46,a4,4a,a6,4e,a8,52,aa,56,ac
  //   ,5a,ae,5e,b0,62,b2,66,b4,6a,b6,6e,b8,72,ba,76,bc,7a,be,7e,c0,82
  //   ,c2,86,c4,8a,c6,8e,c8,92,ca,96,cc,9a,ce,9e,d0,a2,d2,a6,d4,aa,d6
  //   ,ae,d8,b2,da,b6,dc,ba,de,be,e0,c2,e2,c6,e4,ca,e6,ce,e8,d2,ea,d6
  //   ,ec,da,ee,de,f0,e2,f2,e6,f4,ea,f6,ee,f8,f2,fa,f6,fc,fa,fe,fe,0
  //   ,3,6,3,c,f,6,15,18,9,1e,21,c,27,2a,f,30,33,12,39,3c,15,42,45,18
  //   ,4b,4e,1b,54,57,1e,5d,60,21,66,69,24,6f,72,27,78,7b,2a,81,84,2d
  //   ,8a,8d,30,93,96,33,9c,9f,36,a5,a8,39,ae,b1,3c,b7,ba,3f,c0,c3,42
  //   ,c9,cc,45,d2,d5,48,db,de,4b,e4,e7,4e,ed,f0,51,f6,f9,54,ff,2,57
  //   ,8,b,5a,11,14,5d,1a,1d,60,23,26,63,2c,2f,66,35,38,69,3e,41,6c
  //   ,47,4a,6f,50,53,72,59,5c,75,62,65,78,6b,6e,7b,74,77,7e,7d,80,81
  //   ,86,89,84,8f,92,87,98,9b,8a,a1,a4,8d,aa,ad,90,b3,b6,93,bc,bf,96
  //   ,c5,c8,99,ce,d1,9c,d7,da,9f,e0,e3,a2,e9,ec,a5,f2,f5,a8,fb,fe,ab
  //   ,4,7,ae,d,10,b1,16,19,b4,1f,22,b7,28,2b,ba,31,34,bd,3a,3d,c0,43
  //   ,46,c3,4c,4f,c6,55,58,c9,5e,61,cc,67,6a,cf,70,73,d2,79,7c,d5,82
  //   ,85,d8,8b,8e,db,94,97,de,9d,a0,e1,a6,a9,e4,af,b2,e7,b8,bb,ea,c1
  //   ,c4,ed,ca,cd,f0,d3,d6,f3,dc,df,f6,e5,e8,f9,ee,f1,fc,f7,fa,ff,0
  //   ,4,4,c,4,14,c,1c,8,24,14,2c,c,34,1c,3c,10,44,24,4c,14,54,2c,5c
  //   ,18,64,34,6c,1c,74,3c,7c,20,84,44,8c,24,94,4c,9c,28,a4,54,ac,2c
  //   ,b4,5c,bc,30,c4,64,cc,34,d4,6c,dc,38,e4,74,ec,3c,f4,7c,fc,40,4
  //   ,84,c,44,14,8c,1c,48,24,94,2c,4c,34,9c,3c,50,44,a4,4c,54,54,ac
  //   ,5c,58,64,b4,6c,5c,74,bc,7c,60,84,c4,8c,64,94,cc,9c,68,a4,d4,ac
  //   ,6c,b4,dc,bc,70,c4,e4,cc,74,d4,ec,dc,78,e4,f4,ec,7c,f4,fc,fc,80
  //   ,4,4,c,84,14,c,1c,88,24,14,2c,8c,34,1c,3c,90,44,24,4c,94,54,2c
  //   ,5c,98,64,34,6c,9c,74,3c,7c,a0,84,44,8c,a4,94,4c,9c,a8,a4,54,ac,ac
  //   ,b4,5c,bc,b0,c4,64,cc,b4,d4,6c,dc,b8,e4,74,ec,bc,f4,7c,fc,c0,4
  //   ,84,c,c4,14,8c,1c,c8,24,94,2c,cc,34,9c,3c,d0,44,a4,4c,d4,54,ac
  //   ,5c,d8,64,b4,6c,dc,74,bc,7c,e0,84,c4,8c,e4,94,cc,9c,e8,a4,d4,ac
  //   ,ec,b4,dc,bc,f0,c4,e4,cc,f4,d4,ec,dc,f8,e4,f4,ec,fc,f4,fc,fc,0
  //   ,5,a,f,14,5,1e,23,28,2d,a,37,3c,41,46,f,50,55,5a,5f,14,69,6e,73
  //   ,78,19,82,87,8c,91,1e,9b,a0,a5,aa,23,b4,b9,be,c3,28,cd,d2,d7,dc
  //   ,2d,e6,eb,f0,f5,32,ff,4,9,e,37,18,1d,22,27,3c,31,36,3b,40,41,4a
  //   ,4f,54,59,46,63,68,6d,72,4b,7c,81,86,8b,50,95,9a,9f,a4,55,ae,b3
  //   ,b8,bd,5a,c7,cc,d1,d6,5f,e0,e5,ea,ef,64,f9,fe,3,8,69,12,17,1c
  //   ,21,6e,2b,30,35,3a,73,44,49,4e,53,78,5d,62,67,6c,7d,76,7b,80,85
  //   ,82,8f,94,99,9e,87,a8,ad,b2,b7,8c,c1,c6,cb,d0,91,da,df,e4,e9,96
  //   ,f3,f8,fd,2,9b,c,11,16,1b,a0,25,2a,2f,34,a5,3e,43,48,4d,aa,57
  //   ,5c,61,66,af,70,75,7a,7f,b4,89,8e,93,98,b9,a2,a7,ac,b1,be,bb,c0
  //   ,c5,ca,c3,d4,d9,de,e3,c8,ed,f2,f7,fc,cd,6,b,10,15,d2,1f,24,29
  //   ,2e,d7,38,3d,42,47,dc,51,56,5b,60,e1,6a,6f,74,79,e6,83,88,8d,92
  //   ,eb,9c,a1,a6,ab,f0,b5,ba,bf,c4,f5,ce,d3,d8,dd,fa,e7,ec,f1,f6,ff
  //   ,0,6,6,6,c,1e,6,2a,18,12,1e,42,c,4e,2a,1e,30,66,12,72,3c,2a,42
  //   ,8a,18,96,4e,36,54,ae,1e,ba,60,42,66,d2,24,de,72,4e,78,f6,2a,2
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  //   contents of OPS30_0E (hex, n*v repeats v):
  //   641*0,1,0,1,0,1,0,1,0,1,0,1,0,1,0,1,0,1,0,1,0,1,0,1,0,1,0,1,0
  //   ,1,0,1,0,1,0,1,0,1,0,1,0,1,0,1,0,1,0,1,0,1,0,1,0,1,0,1,0,1,0,1
  //   ,0,1,0,1,0,1,0,1,0,1,0,1,0,1,0,1,0,1,0,1,0,1,0,1,0,1,0,1,0,1,0
  //   ,1,0,1,0,1,0,1,0,1,0,1,0,1,0,1,0,1,0,1,0,1,0,1,0,1,0,1,0,1,0,1
  //   ,0,1,0,1,0,1,86*0,1,0,1,1,0,1,1,0,1,1,0,1,1,0,1,1,0,1,1,0,1,1
  //   ,0,1,1,0,1,1,0,1,1,0,1,1,0,1,1,0,1,1,0,1,1,0,1,1,0,1,1,0,1,1,0
  //   ,1,1,0,1,1,0,1,1,0,1,1,0,1,1,0,1,1,0,1,1,0,1,1,0,1,1,0,1,1,0,1,1
  //   ,0,2,2,0,2,2,0,2,2,0,2,2,0,2,2,0,2,2,0,2,2,0,2,2,0,2,2,0,2,2,0
  //   ,2,2,0,2,2,0,2,2,0,2,2,0,2,2,0,2,2,0,2,2,0,2,2,0,2,2,0,2,2,0,2,2
  //   ,0,2,2,0,2,2,0,2,2,0,2,2,0,2,2,0,2,2,0,2,2,66*0,1,0,1,0,1,0,1
  //   ,0,1,0,1,0,1,0,1,0,1,0,1,0,1,0,1,0,1,0,1,0,1,0,1,0,1,0,1,0,1,0
  //   ,1,0,1,0,1,0,1,0,1,0,1,0,1,0,1,0,1,0,1,0,1,0,1,0,1,0,2,1,2,0,2
  //   ,1,2,0,2,1,2,0,2,1,2,0,2,1,2,0,2,1,2,0,2,1,2,0,2,1,2,0,2,1,2,0
  //   ,2,1,2,0,2,1,2,0,2,1,2,0,2,1,2,0,2,1,2,0,2,1,2,0,2,1,2,0,3,1,3
  //   ,0,3,1,3,0,3,1,3,0,3,1,3,0,3,1,3,0,3,1,3,0,3,1,3,0,3,1,3,0,3,1
  //   ,3,0,3,1,3,0,3,1,3,0,3,1,3,0,3,1,3,0,3,1,3,0,3,1,3,0,3,1,3,52*0
  //   ,1,1,1,0,4*1,0,4*1,0,4*1,0,4*1,0,4*1,0,4*1,0,4*1,0,4*1,0,4*1,0
  //   ,1,1,2,2,0,4*2,0,4*2,0,4*2,0,4*2,0,4*2,0,4*2,0,4*2,0,4*2,0,4*2
  //   ,0,2,2,2,3,0,4*3,0,4*3,0,4*3,0,4*3,0,4*3,0,4*3,0,4*3,0,4*3,0,4*3
  //   ,0,4*3,0,4*4,0,4*4,0,4*4,0,4*4,0,4*4,0,4*4,0,4*4,0,4*4,0,4*4,0
  //   ,4*4,44*0,1,0,0,0,1,0,1,0,0,0,1,0,1,0,0,0,1,0,1,0,0,0,1,0,1,0,0,0
  //   ,1,0,1,0,0,0,1,0,1,0,0,0,1,0,1,1,0,1,2,0,2,1,0,1,2,0,2,1,0,1,2
  //   ,0,2,1,0,1,2,0,2,1,0,1,2,0,2,1,0,1,2,0,2,1,0,1,2,0,2,1,1,1,3,0
  //   ,3,1,1,1,3,0,3,1,1,1,3,0,3,1,1,1,3,0,3,1,1,1,3,0,3,1,1,1,3,0,3
  //   ,1,1,1,3,0,3,1,1,2,4,0,4,2,1,2,4,0,4,2,1,2,4,0,4,2,1,2,4,0,4,2
  //   ,1,2,4,0,4,2,1,2,4,0,4,2,1,2,4,0,4,2,1,2,5,0,5,2,1,2,5,0,5,2,1
  //   ,2,5,0,5,2,1,2,5,0,5,2,1,2,5,0,5,2,1,2,5,0,5,2,1,2,5,0,5,2,1,37*0
  //   ,5*1,0,6*1,0,6*1,0,6*1,0,6*1,0,1,1,1,2,2,2,0,6*2,0,6*2,0,6*2,0
  //   ,6*2,0,4*2,3,3,0,6*3,0,6*3,0,6*3,0,6*3,0,6*3,0,6*4,0,6*4,0,6*4
  //   ,0,6*4,0,6*4,0,6*5,0,6*5,0,6*5,0,6*5,0,6*5,0,5,5,4*6,0,6*6,0,6*6
  //   ,0,6*6,0,6*6,0,6,6,6,33*0,1,0,1,0,1,0,1,0,1,0,1,0,1,0,1,0,1,0
  //   ,1,0,1,0,1,0,1,0,1,0,1,0,1,0,2,1,2,0,2,1,2,0,2,1,2,0,2,1,2,0,2
  //   ,1,2,0,2,1,2,0,2,1,2,0,2,1,2,0,3,1,3,0,3,1,3,0,3,1,3,0,3,1,3,0
  //   ,3,1,3,0,3,1,3,0,3,1,3,0,3,1,3,0,4,2,4,1,4,2,4,0,4,2,4,1,4,2,4
  //   ,0,4,2,4,1,4,2,4,0,4,2,4,1,4,2,4,0,5,2,5,1,5,2,5,0,5,2,5,1,5,2
  //   ,5,0,5,2,5,1,5,2,5,0,5,2,5,1,5,2,5,0,6,3,6,1,6,3,6,0,6,3,6,1,6
  //   ,3,6,0,6,3,6,1,6,3,6,0,6,3,6,1,6,3,6,0,7,3,7,1,7,3,7,0,7,3,7,1
  //   ,7,3,7,0,7,3,7,1,7,3,7,0,7,3,7,1,7,3,7,29*0,1,0,1,1,0,1,1,0,1,1
  //   ,0,1,1,0,1,1,0,1,1,0,1,1,0,1,1,0,1,1,0,2,2,0,2,2,0,2,2,0,2,2,0
  //   ,2,2,0,2,2,0,2,2,0,2,2,0,2,2,0,2,3,1,3,3,0,3,3,1,3,3,1,3,3,0,3,3
  //   ,1,3,3,1,3,3,0,3,3,1,3,3,1,4,4,0,4,4,1,4,4,1,4,4,0,4,4,1,4,4,1
  //   ,4,4,0,4,4,1,4,4,1,4,5,0,5,5,1,5,5,1,5,5,0,5,5,1,5,5,1,5,5,0,5,5
  //   ,1,5,5,1,5,5,0,6,6,2,6,6,2,6,6,0,6,6,2,6,6,2,6,6,0,6,6,2,6,6,2
  //   ,6,6,0,6,7,2,7,7,2,7,7,0,7,7,2,7,7,2,7,7,0,7,7,2,7,7,2,7,7,0,7,7
  //   ,2,8,8,2,8,8,0,8,8,2,8,8,2,8,8,0,8,8,2,8,8,2,8,8,0,8,8,2,27*0
  //   ,1,0,1,0,1,0,1,0,0,0,1,0,1,0,1,0,1,0,0,0,1,0,1,0,1,1,2,1,0,1,2
  //   ,1,2,0,2,1,2,1,0,1,2,1,2,0,2,1,2,1,0,1,3,1,3,0,3,1,3,1,0,1,3,1
  //   ,3,0,3,1,3,1,0,1,3,1,3,0,3,1,4,2,0,2,4,2,4,0,4,2,4,2,0,2,4,2,4
  //   ,0,4,2,4,2,0,2,4,2,5,0,5,2,5,2,1,2,5,2,5,0,5,2,5,2,1,2,5,2,5,0
  //   ,5,2,5,3,1,3,6,3,6,0,6,3,6,3,1,3,6,3,6,0,6,3,6,3,1,3,6,3,6,0,7
  //   ,3,7,3,1,3,7,3,7,0,7,3,7,3,1,3,7,3,7,0,7,3,7,3,1,4,8,4,8,0,8,4
  //   ,8,4,1,4,8,4,8,0,8,4,8,4,1,4,8,4,8,0,9,4,9,4,1,4,9,4,9,0,9,4,9
  //   ,4,1,4,9,4,9,0,9,4,9,4,1,24*0,9*1,0,10*1,0,1,1,8*2,0,10*2,0,2,2,2
  //   ,7*3,0,10*3,0,5*3,5*4,0,10*4,0,6*4,4*5,0,10*5,0,7*5,6,6,6,0,10*6
  //   ,0,8*6,7,7,0,10*7,0,10*7,0,10*8,0,10*8,0,10*9,0,10*9,0,9,9*a,0
  //   ,10*a,0,a,a,23*0,1,0,1,0,0,0,1,0,1,0,0,0,1,0,1,0,0,0,1,0,2,0,0
  //   ,1,2,0,2,1,0,0,2,0,2,0,0,1,2,0,2,1,0,0,3,0,3,0,1,1,3,0,3,1,1,0
  //   ,3,0,3,0,1,1,3,0,3,2,1,1,4,0,4,1,1,2,4,0,4,2,1,1,4,0,4,1,1,2,5
  //   ,0,5,2,1,1,5,0,5,1,1,2,5,0,5,2,1,1,5,0,5,1,2,3,6,0,6,3,2,1,6,1
  //   ,6,1,2,3,6,0,6,3,2,1,6,1,7,1,2,3,7,0,7,3,2,1,7,1,7,1,2,3,7,0,7
  //   ,3,2,2,8,1,8,2,2,4,8,0,8,4,2,2,8,1,8,2,2,4,8,0,9,4,3,2,9,1,9,2
  //   ,3,4,9,0,9,4,3,2,9,1,9,2,3,5,a,0,a,5,3,2,a,1,a,2,3,5,a,0,a,5,3
  //   ,2,a,1,b,2,3,5,b,0,b,5,3,2,b,1,b,2,3,5,b,0,b,5,3,20*0,6*1,0,12*1
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endmodule
